# Fritzing sketch RobotArmArduino (saved by Fritzing 0.9.3b)
breadboards: 1

parts:
  Part6 = Arduino Uno (Rev3)
  J2 = Basic Servo
  J3 = Basic Servo
  J4 = Basic Servo
  J5 = Basic Servo
  BT1 = Bluetooth HC-06u [package=THT]
  R1 = Resistor [tolerance=±5% resistance=4.7k package="0805 [SMD]"]
  R2 = Resistor [tolerance=±5% resistance=2.2k package="0805 [SMD]"]
  J6 = Basic Servo

nets:
  N1: Part6.D8, J2.pulse
  N2: Part6.D9_PWM, J3.pulse
  N3: Part6.D10_PWM/SS, J4.pulse
  N4: Part6.D11_PWM/MOSI, J5.pulse
  N5: Part6.D12/MISO, J6.pulse
  GND: Part6.GND, J2.gnd, J3.gnd, J4.gnd, J5.gnd, BT1.GND, R2.Pin_1, J6.gnd
  N6: Part6.D6_PWM, BT1.TXD
  N7: Part6.D7, R1.Pin_1
  VCC: Part6.5V, J2.vcc, J3.vcc, J4.vcc, J5.vcc, BT1.VCC, J6.vcc
  N8: BT1.RXD, R1.Pin_0, R2.Pin_0

notes:
  Z-Rotate Arm
  Y-Lift Arm
  X-Move Arm
  Hand
  Kugelbahn

custom parts:
  Bluetooth HC-06u: Bluetooth HC-06 - face up, pins down 16.5mm x 37.5mm PCB
