# Fritzing sketch RobotArmArduino (saved by Fritzing 0.9.3b)
breadboards: 1

parts:
  Part6 = Arduino Uno (Rev3)
  J2 = Basic Servo
  J3 = Basic Servo
  J4 = Basic Servo
  J5 = Basic Servo
  JACK2 = 2.1mm Barrel Jack with Terminal Block
  BT1 = Bluetooth HC-06u [package=THT]

nets:
  N1: Part6.D8, J2.pulse
  N2: Part6.D9_PWM, J3.pulse
  N3: Part6.D10_PWM/SS, J4.pulse
  N4: Part6.D11_PWM/MOSI, J5.pulse
  GND: Part6.GND, J2.gnd, J3.gnd, J4.gnd, J5.gnd, JACK2.NEG, BT1.GND
  N5: Part6.D6_PWM, BT1.TXD
  N6: Part6.D7, BT1.RXD
  5V: Part6.5V, BT1.VCC
  VCC: J2.vcc, J3.vcc, J4.vcc, J5.vcc, JACK2.POS

custom parts:
  Bluetooth HC-06u: Bluetooth HC-06 - face up, pins down 16.5mm x 37.5mm PCB
